# Fritzing sketch Temperature_Controller (saved by Fritzing 0.9.6b)
perfboards: 3

parts:
  Part3 = Arduino Nano (Rev3.0)  # not connected
  U26 = POT [package=pot_alpha_rv16af-20]
  C6 = Ceramic Capacitor [capacitance=100nF voltage=35V package="100 mil [THT, multilayer]"]
  C7 = Ceramic Capacitor [capacitance=0.1µF voltage=35V package="100 mil [THT, multilayer]"]
  LCD6 = LCD screen  # not connected
  U30 = POT [package=pot_alpha_rv16af-20]
  U31 = POT [package=pot_alpha_rv16af-20]
  U32 = POT [package=pot_alpha_rv16af-20]
  C14 = Ceramic Capacitor [capacitance=0.1µF voltage=35V package="100 mil [THT, multilayer]"]
  C15 = Ceramic Capacitor [capacitance=0.1µF voltage=35V package="100 mil [THT, multilayer]"]
  C16 = Ceramic Capacitor [capacitance=0.1µF voltage=35V package="100 mil [THT, multilayer]"]
  S23 = Pushbutton [package="[THT]"]
  R39 = Resistor [tolerance=±5% resistance=1k power=0.25 package=THT]
  R40 = Resistor [tolerance=±5% resistance=1k power=0.25 package=THT]
  S25 = Pushbutton [package="[THT]"]
  S26 = Pushbutton [package="[THT]"]
  R41 = Resistor [tolerance=±5% resistance=1k power=0.25 package=THT]
  S27 = Pushbutton [package="[THT]"]
  S28 = Pushbutton [package="[THT]"]
  R42 = Resistor [tolerance=±5% resistance=1k power=0.25 package=THT]
  R43 = Resistor [tolerance=±5% resistance=1k power=0.25 package=THT]
  R44 = Resistor [tolerance=±5% resistance=1k power=0.25 package=THT]
  R38 = Resistor [tolerance=±5% power=0.25 resistance=1k package=THT]
  S29 = Pushbutton [package="[THT]"]
  J166 = male pin header, 4 pins [form="♂ (male)"]
  J171 = male pin header, 6 pins [form="♂ (male)"]
  J172 = male pin header, 2 pins [form="♂ (male)"]
  J173 = female pin header, 16 pins [form="♀ (female)"]
  R46 = TRIMPOT [package=trim_pot_pth]
  Q6 = Basic FET N-Channel [package="TO220 [THT]"]
  J231 = female pin header, 3 pins [form="♀ (female)"]
  J232 = female pin header, 1 pin [form="♀ (female)"]
  J233 = female pin header, 15 pins [form="♀ (female)"]
  C21 = Ceramic Capacitor [capacitance=0.1µF voltage=35V package="100 mil [THT, multilayer]"]
  J234 = female pin header, 9 pins [form="♀ (female)"]
  J235 = female pin header, 1 pin [form="♀ (female)"]
  J236 = female pin header, 1 pin [form="♀ (female)"]
  J237 = female pin header, 4 pins [form="♀ (female)"]
  J238 = female pin header, 1 pin [form="♀ (female)"]
  J239 = female pin header, 7 pins [form="♀ (female)"]
  J240 = female pin header, 5 pins [form="♀ (female)"]
  R52 = Resistor [tolerance=±5% power=0.25 resistance=10k package=THT]
  C22 = Ceramic Capacitor [capacitance=0.1µF voltage=35V package="100 mil [THT, multilayer]"]
  J241 = female pin header, 15 pins [form="♀ (female)"]
  J242 = female pin header, 4 pins [form="♀ (female)"]

nets:
  N1: U26.A, C7.1, U30.A, U31.A, U32.A, C14.1, C15.1, C16.1
  N2: U26.E, C7.0, U30.E, U31.E, U32.E, C14.0, C15.0, C16.0
  N3: C6.0, R38.Pin_0, J166.pin4
  N4: C6.1, R38.Pin_1, S29.Pin_1, S29.Pin_2, J166.pin1, J166.pin3
  N5: S23.Pin_1, S23.Pin_2, S25.Pin_3, S25.Pin_4, R42.Pin_0, R42.Pin_1
  N6: S23.Pin_3, S23.Pin_4, R40.Pin_0, R40.Pin_1, S27.Pin_1, S27.Pin_2
  N7: R39.Pin_0, R39.Pin_1, S27.Pin_3, S27.Pin_4, S28.Pin_1, S28.Pin_2
  N8: S25.Pin_1, S25.Pin_2, R41.Pin_0, R41.Pin_1, S29.Pin_3, S29.Pin_4
  N9: S26.Pin_1, S26.Pin_2, S28.Pin_3, S28.Pin_4, R44.Pin_0, R44.Pin_1
  N10: S26.Pin_3, S26.Pin_4, R43.Pin_0, R43.Pin_1
  N11: J171.pin1, J173.pin12
  N12: J171.pin2, J173.pin11
  N13: J171.pin3, J173.pin6
  N14: J171.pin4, J173.pin5
  N15: J171.pin5, J173.pin4
  N16: J171.pin6, J173.pin3
  N17: J172.pin2, R46.CW
  N18: J173.pin1, J173.pin13, J173.pin16
  N19: J173.pin2, J173.pin15, R46.CCW
  N20: J173.pin14, R46.WIPER
  N21: Q6.gate, J233.pin5, R52.Pin_0
  N22: Q6.drain, J231.pin2
  N23: Q6.source, J233.pin12, C21.1, J234.pin3, J236.pin1, J237.pin4, J240.pin1, R52.Pin_1
  N24: J231.pin1, J237.pin2
  N25: J232.pin1, J241.pin6
  N26: J233.pin1, J240.pin4
  N27: J233.pin3, J240.pin5
  N28: J233.pin6, J234.pin9
  N29: J233.pin7, J234.pin8
  N30: J233.pin8, J234.pin7
  N31: J233.pin9, J234.pin6
  N32: J233.pin10, J234.pin5
  N33: J233.pin11, J234.pin4
  N34: C21.0, J234.pin1, J235.pin1, J238.pin1, J239.pin2, J240.pin2, J241.pin12, J242.pin4
  N35: J237.pin1, C22.1, J241.pin15
  N36: J239.pin1, C22.0, J241.pin14, J242.pin3
  N37: J239.pin4, J241.pin11
  N38: J239.pin5, J241.pin10
  N39: J239.pin6, J241.pin9
  N40: J239.pin7, J241.pin8
  N41: J240.pin3, J241.pin1
  N42: J241.pin7, J242.pin1
